# Fritzing sketch Robocar (saved by Fritzing 0.9.3b)
stripboards: 1

parts:
  U1 = ESP8266 NodeMCU LoLin module
  Mod1 = ESP32 - CAM
  Part1 = Arduino Uno (Rev3)
  M1 = DC Motor
  M2 = DC Motor
  GSM_SIM_GPSR_SMS_SIM900_SIM1 = SIM800L [package=THT]
  PIR1 = PIR sensor
  J1 = Basic Servo
  M3 = DC Motor
  M4 = DC Motor
  Part2 = Lithium Ion Cylindrical Battery 3.7v 2200mAh [part_number=1781]
  Part3 = Lithium Ion Cylindrical Battery 3.7v 2200mAh [part_number=1781]
  L298N1 = L298N DC motor driver
  Part4 = Lithium Ion Cylindrical Battery 3.7v 2200mAh [part_number=1781]
  R1 = Resistor [tolerance=±5% resistance=10k package=THT]
  R2 = Resistor [tolerance=±5% resistance=20k package=THT]
  R3 = Resistor [tolerance=±5% resistance=10k package=THT]
  R4 = Resistor [tolerance=±5% resistance=20k package=THT]

nets:
  3V3: U1.3V3, Mod1.3V3, Part1.3V3, PIR1.VDD
  GND: U1.GND, Mod1.GND, Part1.GND, PIR1.GND, J1.gnd, Part3.negative, L298N1.GND, R2.Pin_0, R4.Pin_1
  N1: U1.D8, R3.Pin_0, R4.Pin_0
  N2: Part1.D9_PWM, J1.pulse
  N3: Part1.D2, R1.Pin_1
  N4: Part1.D3_PWM, GSM_SIM_GPSR_SMS_SIM900_SIM1.SIM_TXD
  N5: Part1.D4, L298N1.IN1
  N6: Part1.D5_PWM, L298N1.IN2
  N7: Part1.D6_PWM, L298N1.IN3
  N8: Part1.D7, L298N1.IN4
  5V: Part1.5V, J1.vcc
  N9: M1.pin_1, M2.pin_2, L298N1.OUT3
  N10: M1.pin_2, M2.pin_1, L298N1.OUT4
  N11: GSM_SIM_GPSR_SMS_SIM900_SIM1.5V, Part4.positive
  N12: GSM_SIM_GPSR_SMS_SIM900_SIM1.GND, Part4.negative
  N13: GSM_SIM_GPSR_SMS_SIM900_SIM1.SIM_RXD, R1.Pin_0, R2.Pin_1
  N14: PIR1.SIG, R3.Pin_1
  N15: M3.pin_1, M4.pin_1, L298N1.OUT2
  N16: M3.pin_2, M4.pin_2, L298N1.OUT1
  N17: Part2.positive, L298N1.12V
  N18: Part2.negative, Part3.positive

custom parts:
  ESP8266 NodeMCU LoLin module: ESP8266 based NodeMCU
  ESP32 - CAM: The ESP32-CAM has a very competitive small-size camera module that can operate independently as a minimum system with a footprint of only 27*40.5*4.5mm and a deep sleep current of up to 6mA.
  Lithium Ion Cylindrical Battery 3.7v 2200mAh: This lithium ion battery has a capacity of 2200mAh and a protection circuit that provides over-voltage, under-voltage and over-current protection. This cell can provide 2C of peak current (4400mA). Note that these batteries are not designed to sustain such high loads, we suggest keeping any constant current draw under about 0.5C (1 Amp).
  L298N DC motor driver: 2x DC motor driver with 78M05 positive voltage regulator (7..35 V) L298N: max 46 V, 2 A Set 5 V Enable jumper to enable 5 V regultor (needed for the L298N) and +5 V output at screw terminal or supply external +5 V at screw terminal Set ENA and/or ENB to +5 V to enable motor permanently or supply ENA and/or ENB with PWM signal IN1 and IN2 set rotation directory for motor A (OUT1/OUT2) IN2 and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
